# Fritzing sketch Exercicio 1 (saved by Fritzing 0.9.2b)
breadboards: 1

parts:
  Part1 = Arduino Uno (Rev3)
  DI1 = 7-Segment LED Display [package=THT]
  R1 = Resistor [tolerance=±5% resistance=220 package=THT]
  R2 = Resistor [tolerance=±5% resistance=220 package=THT]
  R3 = Resistor [tolerance=±5% resistance=220 package=THT]
  R4 = Resistor [tolerance=±5% resistance=220 package=THT]
  R5 = Resistor [tolerance=±5% resistance=220 package=THT]

nets:
  N1: Part1.D1/TX, R1.Pin_0
  N2: Part1.D2, R2.Pin_0
  N3: Part1.D3_PWM, R3.Pin_0
  N4: Part1.D4, R4.Pin_0
  N5: Part1.D7, R5.Pin_0
  N6: Part1.5V, DI1.commAnode#7
  N7: DI1.cathodeD, R4.Pin_1
  N8: DI1.cathodeC, R3.Pin_1
  N9: DI1.cathodeB, R2.Pin_1
  N10: DI1.cathodeA, R1.Pin_1
  N11: DI1.cathodeG, R5.Pin_1
