# Fritzing sketch Exercicio 4 (saved by Fritzing 0.9.2b)
breadboards: 1

parts:
  Part1 = Arduino Uno (Rev3)
  DI1 = 7-Segment LED Display [package=THT]
  R1 = Resistor [tolerance=±5% resistance=220 package=THT]
  R2 = Resistor [tolerance=±5% resistance=220 package=THT]
  R3 = Resistor [tolerance=±5% resistance=220 package=THT]
  R4 = Resistor [tolerance=±5% resistance=220 package=THT]
  R5 = Resistor [tolerance=±5% resistance=220 package=THT]
  R6 = Resistor [tolerance=±5% resistance=220 package=THT]
  R7 = Resistor [tolerance=±5% resistance=220 package=THT]
  S1 = Pushbutton [package=THT]
  S2 = Pushbutton [package=THT]

nets:
  N1: Part1.D8, R2.Pin_0
  N2: Part1.D9_PWM, R3.Pin_0
  N3: Part1.D1/TX, R1.Pin_0
  N4: Part1.D2, S1.leg1
  N5: Part1.D3_PWM, S2.leg1
  N6: Part1.D4, R4.Pin_0
  N7: Part1.D5_PWM, R5.Pin_0
  N8: Part1.D6_PWM, R6.Pin_0
  N9: Part1.D7, R7.Pin_0
  N10: Part1.5V, DI1.commAnode#7
  N11: Part1.GND, S1.leg0, S2.leg0
  N12: DI1.cathodeE, R5.Pin_1
  N13: DI1.cathodeD, R4.Pin_1
  N14: DI1.cathodeC, R3.Pin_1
  N15: DI1.cathodeB, R2.Pin_1
  N16: DI1.cathodeA, R1.Pin_1
  N17: DI1.cathodeF, R6.Pin_1
  N18: DI1.cathodeG, R7.Pin_1
